# Fritzing sketch interface (saved by Fritzing 0.9.3b)

parts:
  Bauteil1 = Arduino Mega 2560 (Rev3)
  J2 = shrouded pin header, 6 pins [form="♂ (shrouded male)"]
  R3 = Resistor [tolerance=±5% resistance=10k package=THT]
  U2 = Sharp PC817 [package=THT]
  R4 = Resistor [tolerance=±5% resistance=560 package=THT]
  R5 = Resistor [tolerance=±5% resistance=560 package=THT]

nets:
  N1: Bauteil1.D19/RX1, J2.pin1, R3.Pin_1
  N2: Bauteil1.D18/TX1, U2.Pin_1
  N3: Bauteil1.GND, J2.pin3, U2.Pin_3, R5.Pin_1
  N4: Bauteil1.5V, R3.Pin_0, R4.Pin_1
  N5: J2.pin2, U2.Pin_4, R4.Pin_0
  N6: U2.Pin_2, R5.Pin_0
