# Fritzing sketch interface (saved by Fritzing 0.9.3b)

parts:
  Bauteil1 = Arduino Mega 2560 (Rev3)
  J2 = shrouded pin header, 6 pins [form="♂ (shrouded male)"]
  R3 = Resistor [tolerance=±5% resistance=10k package=THT]
  PNP = PNP-Transistor [package="TO92 [THT]"]
  R6 = Resistor [tolerance=±5% resistance=5 package=THT]
  R7 = Resistor [tolerance=±5% resistance=10 package=THT]
  R8 = Resistor [tolerance=±5% resistance=1k package=THT]

nets:
  N1: Bauteil1.D19/RX1, J2.pin4, R3.Pin_1
  N2: Bauteil1.D18/TX1, R8.Pin_0
  N3: Bauteil1.GND, J2.pin6, R7.Pin_0
  N4: Bauteil1.5V, R3.Pin_0, R6.Pin_0
  N5: J2.pin5, PNP.C, R7.Pin_1
  N6: PNP.E, R6.Pin_1
  N7: PNP.B, R8.Pin_1
